# Fritzing sketch Controller_Sketch (saved by Fritzing 0.9.3b)
breadboards: 1

parts:
  부품1 = Arduino Uno (Rev3)
  S1 = Pushbutton [package="[THT]"]
  S3 = Pushbutton [package="[THT]"]
  R1 = Resistor [tolerance=±5% resistance=220 package=THT]
  R2 = Resistor [tolerance=±5% resistance=220 package=THT]
  R3 = Resistor [tolerance=±5% resistance=220 package=THT]
  LED1 = LED - 5mm [color="Red (633nm)" package="5 mm [THT]"]
  LED2 = LED - 5mm [color="Green (555nm)" package="5 mm [THT]"]
  LED3 = LED - 5mm [color="Red (633nm)" package="5 mm [THT]"]
  J1 = Piezo Speaker
  R4 = Resistor [tolerance=±5% resistance=10k package=THT]
  R6 = Resistor [tolerance=±5% resistance=10k package=THT]
  S4 = Pushbutton [package="[THT]"]
  R7 = Resistor [tolerance=±5% resistance=10k package=THT]

nets:
  N1: 부품1.D8, LED2.cathode
  N2: 부품1.D9_PWM, LED1.cathode
  N3: 부품1.D10_PWM/SS, S4.Pin_1, S4.Pin_2, R7.Pin_0
  N4: 부품1.D11_PWM/MOSI, S1.Pin_1, S1.Pin_2, R4.Pin_0
  N5: 부품1.GND, R1.Pin_1, R2.Pin_1, R3.Pin_1, J1.pin2, R4.Pin_1, R6.Pin_1, R7.Pin_1
  N6: 부품1.D4, S3.Pin_1, S3.Pin_2, R6.Pin_0
  N7: 부품1.D5_PWM, J1.pin1
  N8: 부품1.D7, LED3.cathode
  N9: 부품1.5V, S1.Pin_3, S1.Pin_4, S3.Pin_3, S3.Pin_4, S4.Pin_3, S4.Pin_4
  N10: R1.Pin_0, LED1.anode
  N11: R2.Pin_0, LED2.anode
  N12: R3.Pin_0, LED3.anode
